// Logisim project circuitQuest1.circ as structural Verilog: 1 circuit, main circuit main
module main (
  input  A,
  input  B,
  input  A_2,
  input  B_2,
  output out_5
);

  wire and_1_out, nor_1_out, or_1_out;

  and and_1 (and_1_out, A, B);
  or or_1 (or_1_out, A_2, B_2);
  nor nor_1 (nor_1_out, and_1_out, or_1_out);
  not not_1 (out_5, nor_1_out);
endmodule
